// Logisim project 1713177_dld.circ as structural Verilog: 1 circuit, main circuit main
module main (
  input  in_1,
  input  in_2,
  input  in_3,
  input  in_4,
  input  in_5,
  input  in_6,
  input  in_7,
  input  in_8,
  input  in_9,
  input  in_10,
  input  in_11,
  input  in_12,
  input  in_13,
  input  in_14,
  input  in_15,
  input  in_16,
  input  in_17,
  input  in_18,
  input  in_19,
  input  in_20,
  input  in_21,
  output out_22,
  output out_23
);

  wire and_1_out, and_2_out, and_3_out, and_4_out, and_5_out, and_6_out, not_1_out, xnor_1_out, xnor_2_out,
       xnor_3_out, xnor_4_out, xnor_5_out, xnor_6_out, xnor_7_out, xnor_8_out, xnor_9_out, xnor_10_out;

  xnor xnor_1 (xnor_1_out, in_1, in_11);
  xnor xnor_2 (xnor_2_out, in_2, in_12);
  xnor xnor_3 (xnor_3_out, in_3, in_13);
  xnor xnor_4 (xnor_4_out, in_4, in_14);
  xnor xnor_5 (xnor_5_out, in_5, in_15);
  xnor xnor_6 (xnor_6_out, in_6, in_16);
  xnor xnor_7 (xnor_7_out, in_7, in_17);
  xnor xnor_8 (xnor_8_out, in_8, in_20);
  xnor xnor_9 (xnor_9_out, in_9, in_21);
  not xnor_10 (xnor_10_out, in_10);  // XNOR_Gate
  and and_1 (and_1_out, xnor_1_out, xnor_2_out);
  and and_2 (and_2_out, xnor_3_out, xnor_4_out);
  and and_3 (and_3_out, xnor_5_out, xnor_6_out);
  and and_4 (and_4_out, xnor_7_out, xnor_8_out);
  and and_5 (and_5_out, xnor_9_out, xnor_10_out);
  and and_6 (and_6_out, and_1_out, and_2_out, and_3_out, and_4_out, and_5_out);
  and and_7 (out_22, and_6_out, in_18);
  not not_1 (not_1_out, and_6_out);
  and and_8 (out_23, not_1_out, in_18);
  LED led_1 (.in(out_22));
  LED led_2 (.in(out_23));
endmodule
